// Logisim project ALU.circ as structural Verilog: 42 circuits, main circuit main
// NOT
module main (
  input  A,
  output result
);

  Transistor transistor_1 (.in(1'b1), .out(result), .gate(A));
  Transistor #(.\type ("n")) transistor_2 (.in(1'b0), .out(result), .gate(A));
endmodule

module NOT_GATE (
  input  in_1,
  output out_2
);

  Transistor transistor_1 (.in(1'b1), .out(out_2), .gate(in_1));
  Transistor #(.\type ("n")) transistor_2 (.in(1'b0), .out(out_2), .gate(in_1));
endmodule

module NAND_GATE (
  input  A,
  input  B,
  output result
);

  wire transistor_4_out;

  Transistor transistor_1 (.in(1'b1), .out(result), .gate(A));
  Transistor transistor_2 (.in(1'b1), .out(result), .gate(B));
  Transistor #(.\type ("n")) transistor_3 (.in(transistor_4_out), .out(result), .gate(A));
  Transistor #(.\type ("n")) transistor_4 (.in(1'b0), .out(transistor_4_out), .gate(B));
endmodule

module AND_GATE (
  input  A,
  input  B,
  output result
);

  wire transistor_1_out, transistor_3_out;

  Transistor transistor_1 (.in(1'b1), .out(transistor_1_out), .gate(B));
  Transistor #(.\type ("n")) transistor_2 (.in(transistor_3_out), .out(transistor_1_out), .gate(B));
  Transistor #(.\type ("n")) transistor_3 (.in(1'b0), .out(transistor_3_out), .gate(A));
  Transistor transistor_4 (.in(1'b1), .out(transistor_1_out), .gate(A));
  Transistor transistor_5 (.in(1'b1), .out(result), .gate(transistor_1_out));
  Transistor #(.\type ("n")) transistor_6 (.in(1'b0), .out(result), .gate(transistor_1_out));
endmodule

module NOR_GATE (
  input  A,
  input  B,
  output result
);

  wire transistor_1_out;

  Transistor transistor_1 (.in(1'b1), .out(transistor_1_out), .gate(A));
  Transistor transistor_2 (.in(transistor_1_out), .out(result), .gate(B));
  Transistor #(.\type ("n")) transistor_3 (.in(1'b0), .out(result), .gate(A));
  Transistor #(.\type ("n")) transistor_4 (.in(1'b0), .out(result), .gate(B));
endmodule

module OR_GATE (
  input  A,
  input  B,
  output out_3
);

  wire transistor_1_out, transistor_2_out;

  Transistor #(.\type ("n")) transistor_1 (.in(1'b0), .out(transistor_1_out), .gate(A));
  Transistor transistor_2 (.in(1'b1), .out(transistor_2_out), .gate(A));
  Transistor transistor_3 (.in(transistor_2_out), .out(transistor_1_out), .gate(B));
  Transistor #(.\type ("n")) transistor_4 (.in(1'b0), .out(transistor_1_out), .gate(B));
  Transistor transistor_5 (.in(1'b1), .out(out_3), .gate(transistor_1_out));
  Transistor #(.\type ("n")) transistor_6 (.in(1'b0), .out(out_3), .gate(transistor_1_out));
endmodule

module XOR_GATE (
  input  A,
  input  B,
  output result
);

  wire nand_gate_1_result, nand_gate_2_result, nand_gate_3_result;

  NAND_GATE nand_gate_1 (.A(A), .B(B), .result(nand_gate_1_result));
  NAND_GATE nand_gate_2 (.A(A), .B(nand_gate_1_result), .result(nand_gate_2_result));
  NAND_GATE nand_gate_3 (.A(nand_gate_1_result), .B(B), .result(nand_gate_3_result));
  NAND_GATE nand_gate_4 (.A(nand_gate_2_result), .B(nand_gate_3_result), .result(result));
endmodule

module XNOR_GATE (
  input  A,
  input  B,
  output result
);

  wire xor_gate_1_result;

  XOR_GATE xor_gate_1 (.A(A), .B(B), .result(xor_gate_1_result));
  NOT_GATE not_gate_1 (.in_1(xor_gate_1_result), .out_2(result));
endmodule

module HALF_ADDER (
  input  A,
  input  B,
  output sum,
  output carry
);

  XOR_GATE xor_gate_1 (.A(A), .B(B), .result(sum));
  AND_GATE and_gate_1 (.A(A), .B(B), .result(carry));
endmodule

module ODD (
  input  A,
  input  B,
  input  CARRY_IN,
  output SUM
);

  wire xor_gate_1_result;

  XOR_GATE xor_gate_1 (.A(A), .B(B), .result(xor_gate_1_result));
  XOR_GATE xor_gate_2 (.A(xor_gate_1_result), .B(CARRY_IN), .result(SUM));
endmodule

module MAJ (
  input  A,
  input  B,
  input  CARRY_IN,
  output result
);

  wire and_gate_1_result, and_gate_2_result, xor_gate_1_result;

  AND_GATE and_gate_1 (.A(A), .B(B), .result(and_gate_1_result));
  XOR_GATE xor_gate_1 (.A(A), .B(B), .result(xor_gate_1_result));
  AND_GATE and_gate_2 (.A(xor_gate_1_result), .B(CARRY_IN), .result(and_gate_2_result));
  OR_GATE or_gate_1 (.A(and_gate_1_result), .B(and_gate_2_result), .out_3(result));
endmodule

module Full_adder (
  input  A,
  input  B,
  input  CARRY_IN,
  output SUM,
  output CARRY_OUT
);

  ODD odd_1 (.A(A), .B(B), .CARRY_IN(CARRY_IN), .SUM(SUM));
  MAJ maj_1 (.A(A), .B(B), .CARRY_IN(CARRY_IN), .result(CARRY_OUT));
endmodule

module ADDER_8_BIT (
  input  [7:0] A,
  input  carry,
  input  [7:0] B,
  output [7:0] SUM
);

  wire full_adder_1_carry_out, full_adder_2_carry_out, full_adder_3_carry_out, full_adder_4_carry_out,
       full_adder_5_carry_out, full_adder_6_carry_out, full_adder_7_carry_out;

  // Probe on A
  // Probe on B
  Full_adder full_adder_1 (.A(A[0]), .B(B[0]), .CARRY_IN(carry), .SUM(SUM[0]), .CARRY_OUT(full_adder_1_carry_out));
  Full_adder full_adder_2 (
    .A(A[1]), .B(B[1]), .CARRY_IN(full_adder_1_carry_out), .SUM(SUM[1]), .CARRY_OUT(full_adder_2_carry_out));
  Full_adder full_adder_3 (
    .A(A[2]), .B(B[2]), .CARRY_IN(full_adder_2_carry_out), .SUM(SUM[2]), .CARRY_OUT(full_adder_3_carry_out));
  Full_adder full_adder_4 (
    .A(A[3]), .B(B[3]), .CARRY_IN(full_adder_3_carry_out), .SUM(SUM[3]), .CARRY_OUT(full_adder_4_carry_out));
  Full_adder full_adder_5 (
    .A(A[4]), .B(B[4]), .CARRY_IN(full_adder_4_carry_out), .SUM(SUM[4]), .CARRY_OUT(full_adder_5_carry_out));
  Full_adder full_adder_6 (
    .A(A[5]), .B(B[5]), .CARRY_IN(full_adder_5_carry_out), .SUM(SUM[5]), .CARRY_OUT(full_adder_6_carry_out));
  Full_adder full_adder_7 (
    .A(A[6]), .B(B[6]), .CARRY_IN(full_adder_6_carry_out), .SUM(SUM[6]), .CARRY_OUT(full_adder_7_carry_out));
  Full_adder full_adder_8 (.A(A[7]), .B(B[7]), .CARRY_IN(full_adder_7_carry_out), .SUM(SUM[7]));  // open: CARRY_OUT
  // Probe on SUM
endmodule

module AND_8BIT (
  input  [7:0] A,
  input  [7:0] B,
  output [7:0] result
);

  AND_GATE and_gate_1 (.A(A[0]), .B(B[0]), .result(result[0]));
  AND_GATE and_gate_2 (.A(A[1]), .B(B[1]), .result(result[1]));
  AND_GATE and_gate_3 (.A(A[2]), .B(B[2]), .result(result[2]));
  AND_GATE and_gate_4 (.A(A[3]), .B(B[3]), .result(result[3]));
  AND_GATE and_gate_5 (.A(A[4]), .B(B[4]), .result(result[4]));
  AND_GATE and_gate_6 (.A(A[5]), .B(B[5]), .result(result[5]));
  AND_GATE and_gate_7 (.A(A[6]), .B(B[6]), .result(result[6]));
  AND_GATE and_gate_8 (.A(A[7]), .B(B[7]), .result(result[7]));
endmodule

module XOR_8BIT (
  input  [7:0] A,
  input  [7:0] B,
  output [7:0] result
);

  XOR_GATE xor_gate_1 (.A(A[0]), .B(B[0]), .result(result[0]));
  XOR_GATE xor_gate_2 (.A(A[1]), .B(B[1]), .result(result[1]));
  XOR_GATE xor_gate_3 (.A(A[2]), .B(B[2]), .result(result[2]));
  XOR_GATE xor_gate_4 (.A(A[3]), .B(B[3]), .result(result[3]));
  XOR_GATE xor_gate_5 (.A(A[4]), .B(B[4]), .result(result[4]));
  XOR_GATE xor_gate_6 (.A(A[5]), .B(B[5]), .result(result[5]));
  XOR_GATE xor_gate_7 (.A(A[6]), .B(B[6]), .result(result[6]));
  XOR_GATE xor_gate_8 (.A(A[7]), .B(B[7]), .result(result[7]));
endmodule

module AND_3INPUT (
  input  A,
  input  B,
  input  C,
  output RESULT
);

  wire and_gate_1_result;

  AND_GATE and_gate_1 (.A(A), .B(B), .result(and_gate_1_result));
  AND_GATE and_gate_2 (.A(and_gate_1_result), .B(C), .result(RESULT));
endmodule

module decorder3_8 (
  input  A,
  input  B,
  input  C,
  output s1,
  output s2,
  output s3,
  output s4,
  output s5,
  output s6,
  output s7,
  output s8
);

  wire not_gate_1_out_2, not_gate_2_out_2, not_gate_3_out_2;

  NOT_GATE not_gate_1 (.in_1(A), .out_2(not_gate_1_out_2));
  NOT_GATE not_gate_2 (.in_1(B), .out_2(not_gate_2_out_2));
  NOT_GATE not_gate_3 (.in_1(C), .out_2(not_gate_3_out_2));
  AND_3INPUT and_3input_1 (.A(not_gate_1_out_2), .B(not_gate_2_out_2), .C(not_gate_3_out_2), .RESULT(s1));
  AND_3INPUT and_3input_2 (.A(not_gate_1_out_2), .B(not_gate_2_out_2), .C(C), .RESULT(s2));
  AND_3INPUT and_3input_3 (.A(not_gate_1_out_2), .B(B), .C(not_gate_3_out_2), .RESULT(s3));
  AND_3INPUT and_3input_4 (.A(not_gate_1_out_2), .B(B), .C(C), .RESULT(s4));
  AND_3INPUT and_3input_5 (.A(A), .B(not_gate_2_out_2), .C(not_gate_3_out_2), .RESULT(s5));
  AND_3INPUT and_3input_6 (.A(A), .B(not_gate_2_out_2), .C(C), .RESULT(s6));
  AND_3INPUT and_3input_7 (.A(A), .B(B), .C(not_gate_3_out_2), .RESULT(s7));
  AND_3INPUT and_3input_8 (.A(A), .B(B), .C(C), .RESULT(s8));
endmodule

module demux3_8 (
  input  Singal,
  input  A,
  input  B,
  input  C,
  output s1,
  output s2,
  output s3,
  output s4,
  output s5,
  output s6,
  output s7,
  output s8
);

  wire decorder3_8_1_s1, decorder3_8_1_s2, decorder3_8_1_s3, decorder3_8_1_s4, decorder3_8_1_s5,
       decorder3_8_1_s6, decorder3_8_1_s7, decorder3_8_1_s8;

  decorder3_8 decorder3_8_1 (
    .A(A), .B(B), .C(C), .s1(decorder3_8_1_s1), .s2(decorder3_8_1_s2), .s3(decorder3_8_1_s3),
    .s4(decorder3_8_1_s4), .s5(decorder3_8_1_s5), .s6(decorder3_8_1_s6), .s7(decorder3_8_1_s7),
    .s8(decorder3_8_1_s8));
  AND_GATE and_gate_1 (.A(decorder3_8_1_s1), .B(Singal), .result(s1));
  AND_GATE and_gate_2 (.A(decorder3_8_1_s2), .B(Singal), .result(s2));
  AND_GATE and_gate_3 (.A(decorder3_8_1_s3), .B(Singal), .result(s3));
  AND_GATE and_gate_4 (.A(decorder3_8_1_s4), .B(Singal), .result(s4));
  AND_GATE and_gate_5 (.A(decorder3_8_1_s5), .B(Singal), .result(s5));
  AND_GATE and_gate_6 (.A(decorder3_8_1_s6), .B(Singal), .result(s6));
  AND_GATE and_gate_7 (.A(decorder3_8_1_s7), .B(Singal), .result(s7));
  AND_GATE and_gate_8 (.A(decorder3_8_1_s8), .B(Singal), .result(s8));
endmodule

module decordANDmux (
  input  DATA_IN,
  input  A,
  input  B,
  input  C,
  output S1_1,
  output S1_X,
  output S2_1,
  output S2_X,
  output S3_1,
  output S3_X,
  output S4_1,
  output S4_X,
  output S5_1,
  output S5_X,
  output S6_1,
  output S6_X,
  output S7_1,
  output S7_X,
  output S8_1,
  output S8_X
);

  decorder3_8 decorder3_8_1 (
    .A(A), .B(B), .C(C), .s1(S1_1), .s2(S2_1), .s3(S3_1), .s4(S4_1), .s5(S5_1), .s6(S6_1), .s7(S7_1),
    .s8(S8_1));
  AND_GATE and_gate_1 (.A(S1_1), .B(DATA_IN), .result(S1_X));
  AND_GATE and_gate_2 (.A(S2_1), .B(DATA_IN), .result(S2_X));
  AND_GATE and_gate_3 (.A(S3_1), .B(DATA_IN), .result(S3_X));
  AND_GATE and_gate_4 (.A(S4_1), .B(DATA_IN), .result(S4_X));
  AND_GATE and_gate_5 (.A(S5_1), .B(DATA_IN), .result(S5_X));
  AND_GATE and_gate_6 (.A(S6_1), .B(DATA_IN), .result(S6_X));
  AND_GATE and_gate_7 (.A(S7_1), .B(DATA_IN), .result(S7_X));
  AND_GATE and_gate_8 (.A(S8_1), .B(DATA_IN), .result(S8_X));
endmodule

module OR_8BIT (
  input  [7:0] A,
  input  [7:0] B,
  output [7:0] Result
);

  OR_GATE or_gate_1 (.A(A[0]), .B(B[0]), .out_3(Result[0]));
  OR_GATE or_gate_2 (.A(A[1]), .B(B[1]), .out_3(Result[1]));
  OR_GATE or_gate_3 (.A(A[2]), .B(B[2]), .out_3(Result[2]));
  OR_GATE or_gate_4 (.A(A[3]), .B(B[3]), .out_3(Result[3]));
  OR_GATE or_gate_5 (.A(A[4]), .B(B[4]), .out_3(Result[4]));
  OR_GATE or_gate_6 (.A(A[5]), .B(B[5]), .out_3(Result[5]));
  OR_GATE or_gate_7 (.A(A[6]), .B(B[6]), .out_3(Result[6]));
  OR_GATE or_gate_8 (.A(A[7]), .B(B[7]), .out_3(Result[7]));
endmodule

module OR_3input (
  input  [7:0] A,
  input  [7:0] B,
  input  [7:0] C,
  output [7:0] result
);

  wire [7:0] or_8bit_1_result;

  OR_8BIT or_8bit_1 (.A(A), .B(B), .Result(or_8bit_1_result));
  OR_8BIT or_8bit_2 (.A(or_8bit_1_result), .B(C), .Result(result));
endmodule

module ONE_hot_mux (
  input  add,
  input  sub,
  input  xor_b,
  input  and_b,
  input  r_shift,
  input  l_shift,
  input  sel_add,
  input  sel_sub,
  input  sel_xor,
  input  sel_and,
  input  sel_Rshift,
  input  sel_Lshift,
  output mux_out
);

  wire and_gate_1_result, and_gate_2_result, and_gate_3_result, and_gate_4_result, and_gate_5_result,
       and_gate_6_result;

  AND_GATE and_gate_1 (.A(add), .B(sel_add), .result(and_gate_1_result));
  AND_GATE and_gate_2 (.A(sub), .B(sel_sub), .result(and_gate_2_result));
  AND_GATE and_gate_3 (.A(xor_b), .B(sel_xor), .result(and_gate_3_result));
  AND_GATE and_gate_4 (.A(and_b), .B(sel_and), .result(and_gate_4_result));
  AND_GATE and_gate_5 (.A(r_shift), .B(sel_Rshift), .result(and_gate_5_result));
  AND_GATE and_gate_6 (.A(l_shift), .B(sel_Lshift), .result(and_gate_6_result));
  or or_1 (mux_out, and_gate_1_result, and_gate_2_result, and_gate_3_result, and_gate_4_result, and_gate_5_result, and_gate_6_result);
endmodule

module hot_8_mux (
  input  sel_add,
  input  sel_sub,
  input  sel_xor,
  input  sel_and,
  input  sel_Rshift,
  input  sel_Lshift,
  input  [7:0] add,
  input  [7:0] l_shift,
  input  [7:0] and_b,
  input  [7:0] r_shift,
  input  [7:0] sub,
  input  [7:0] xor_in,
  output [7:0] resul
);

  ONE_hot_mux one_hot_mux_1 (
    .add(add[0]), .sub(sub[0]), .xor_b(xor_in[0]), .and_b(and_b[0]), .r_shift(r_shift[0]),
    .l_shift(l_shift[0]), .sel_add(sel_add), .sel_sub(sel_sub), .sel_xor(sel_xor), .sel_and(sel_and),
    .sel_Rshift(sel_Rshift), .sel_Lshift(sel_Lshift), .mux_out(resul[0]));
  ONE_hot_mux one_hot_mux_2 (
    .add(add[1]), .sub(sub[1]), .xor_b(xor_in[1]), .and_b(and_b[1]), .r_shift(r_shift[1]),
    .l_shift(l_shift[1]), .sel_add(sel_add), .sel_sub(sel_sub), .sel_xor(sel_xor), .sel_and(sel_and),
    .sel_Rshift(sel_Rshift), .sel_Lshift(sel_Lshift), .mux_out(resul[1]));
  ONE_hot_mux one_hot_mux_3 (
    .add(add[2]), .sub(sub[2]), .xor_b(xor_in[2]), .and_b(and_b[2]), .r_shift(r_shift[2]),
    .l_shift(l_shift[2]), .sel_add(sel_add), .sel_sub(sel_sub), .sel_xor(sel_xor), .sel_and(sel_and),
    .sel_Rshift(sel_Rshift), .sel_Lshift(sel_Lshift), .mux_out(resul[2]));
  ONE_hot_mux one_hot_mux_4 (
    .add(add[3]), .sub(sub[3]), .xor_b(xor_in[3]), .and_b(and_b[3]), .r_shift(r_shift[3]),
    .l_shift(l_shift[3]), .sel_add(sel_add), .sel_sub(sel_sub), .sel_xor(sel_xor), .sel_and(sel_and),
    .sel_Rshift(sel_Rshift), .sel_Lshift(sel_Lshift), .mux_out(resul[3]));
  ONE_hot_mux one_hot_mux_5 (
    .add(add[4]), .sub(sub[4]), .xor_b(xor_in[4]), .and_b(and_b[4]), .r_shift(r_shift[4]),
    .l_shift(l_shift[4]), .sel_add(sel_add), .sel_sub(sel_sub), .sel_xor(sel_xor), .sel_and(sel_and),
    .sel_Rshift(sel_Rshift), .sel_Lshift(sel_Lshift), .mux_out(resul[4]));
  ONE_hot_mux one_hot_mux_6 (
    .add(add[5]), .sub(sub[5]), .xor_b(xor_in[5]), .and_b(and_b[5]), .r_shift(r_shift[5]),
    .l_shift(l_shift[5]), .sel_add(sel_add), .sel_sub(sel_sub), .sel_xor(sel_xor), .sel_and(sel_and),
    .sel_Rshift(sel_Rshift), .sel_Lshift(sel_Lshift), .mux_out(resul[5]));
  ONE_hot_mux one_hot_mux_7 (
    .add(add[6]), .sub(sub[6]), .xor_b(xor_in[6]), .and_b(and_b[6]), .r_shift(r_shift[6]),
    .l_shift(l_shift[6]), .sel_add(sel_add), .sel_sub(sel_sub), .sel_xor(sel_xor), .sel_and(sel_and),
    .sel_Rshift(sel_Rshift), .sel_Lshift(sel_Lshift), .mux_out(resul[6]));
  ONE_hot_mux one_hot_mux_8 (
    .add(add[7]), .sub(sub[7]), .xor_b(xor_in[7]), .and_b(and_b[7]), .r_shift(r_shift[7]),
    .l_shift(l_shift[7]), .sel_add(sel_add), .sel_sub(sel_sub), .sel_xor(sel_xor), .sel_and(sel_and),
    .sel_Rshift(sel_Rshift), .sel_Lshift(sel_Lshift), .mux_out(resul[7]));
endmodule

module l_shift (
  input  [7:0] A,
  output [7:0] result
);


  assign result = {A[6:0], 1'b0};
endmodule

module R_shift (
  input  [7:0] A,
  output [7:0] result
);


  assign result = {1'b0, A[7:1]};
endmodule

module sub_8 (
  input  [7:0] A,
  input  [7:0] B,
  output [7:0] result
);

  wire [7:0] xor_8bit_1_result;

  XOR_8BIT xor_8bit_1 (.A(B), .B({8{1'b1}}), .result(xor_8bit_1_result));
  ADDER_8_BIT adder_8_bit_1 (.A(A), .carry(1'b1), .B(xor_8bit_1_result), .SUM(result));
endmodule

module MILESTONE (
  input  [7:0] A,
  input  [7:0] B,
  input  add,
  input  sub,
  input  xor_r,
  input  AND_R,
  input  r_shift_r,
  input  L_shift_r,
  output [7:0] result
);

  wire [7:0] adder_8_bit_1_sum, and_8bit_1_result, l_shift_1_result, r_shift_1_result, sub_8_1_result,
       xor_8bit_1_result;

  ADDER_8_BIT adder_8_bit_1 (.A(A), .B(B), .SUM(adder_8_bit_1_sum));  // open: carry
  sub_8 sub_8_1 (.A(A), .B(B), .result(sub_8_1_result));
  XOR_8BIT xor_8bit_1 (.A(A), .B(B), .result(xor_8bit_1_result));
  AND_8BIT and_8bit_1 (.A(A), .B(B), .result(and_8bit_1_result));
  R_shift r_shift_1 (.A(A), .result(r_shift_1_result));
  l_shift l_shift_1 (.A(A), .result(l_shift_1_result));
  hot_8_mux hot_8_mux_1 (
    .sel_add(add), .sel_sub(sub), .sel_xor(xor_r), .sel_and(AND_R), .sel_Rshift(r_shift_r),
    .sel_Lshift(L_shift_r), .add(adder_8_bit_1_sum), .l_shift(l_shift_1_result), .and_b(and_8bit_1_result),
    .r_shift(r_shift_1_result), .sub(sub_8_1_result), .xor_in(xor_8bit_1_result), .resul(result));
endmodule

module FINAL (
  input  [7:0] A,
  input  [7:0] B,
  input  ADD,
  input  SUB,
  input  XOR_r,
  input  AND_r,
  input  R_shift_r,
  input  L_shift_l,
  output [7:0] out_9
);

  // Probe on A
  // Probe on B
  MILESTONE milestone_1 (
    .A(A), .B(B), .add(ADD), .sub(SUB), .xor_r(XOR_r), .AND_R(AND_r), .r_shift_r(R_shift_r),
    .L_shift_r(L_shift_l), .result(out_9));
  // Probe on out_9
endmodule

module srlatch (
  input  S,
  input  R,
  output out_3
);

  wire nor_2_out;

  nor nor_1 (out_3, S, nor_2_out);
  nor nor_2 (nor_2_out, R, out_3);
endmodule

module flipflop (
  input  Data,
  input  CLK,
  output Q
);

  wire nand_1_out, nand_2_out, not_1_out;

  not not_1 (not_1_out, Data);
  nand nand_1 (nand_1_out, Data, CLK);
  nand nand_2 (nand_2_out, not_1_out, CLK);
  srlatch srlatch_1 (.S(nand_1_out), .R(nand_2_out), .out_3(Q));
endmodule

module memoryclk (
  input  clt,
  input  Data,
  output Q
);

  D_Flip_Flop d_ff_1 (.D(Data), .clk(clt), .Q(Q));  // open: Qn, preset, reset
endmodule

module memotybit (
  input  DATA,
  input  CLK,
  output out_3
);

  wire and_1_out, and_2_out, not_1_out;

  not not_1 (not_1_out, DATA);
  and and_1 (and_1_out, CLK, not_1_out);
  and and_2 (and_2_out, DATA, CLK);
  srlatch srlatch_1 (.S(and_1_out), .R(and_2_out), .out_3(out_3));
endmodule

module clock_control (
  input  RUN,
  input  halt,
  output Cl,
  output fetch,
  output fetch_w,
  output execute,
  output execute_w
);

  wire clock_1_out, not_1_out;

  Clock clock_1 (.out(clock_1_out));
  and and_1 (Cl, RUN, clock_1_out, halt);
  D_Flip_Flop d_ff_1 (.D(not_1_out), .clk(Cl), .Q(execute));  // open: Qn, preset, reset
  not not_1 (not_1_out, execute);
  not not_2 (fetch, execute);
  and and_2 (fetch_w, fetch, Cl);
  and and_3 (execute_w, execute, Cl);
endmodule

module reg8bit (
  input  write,
  input  [7:0] Data,
  output [7:0] Q
);

  memoryclk memoryclk_1 (.clt(write), .Data(Data[6]), .Q(Q[6]));
  memoryclk memoryclk_2 (.clt(write), .Data(Data[0]), .Q(Q[0]));
  memoryclk memoryclk_3 (.clt(write), .Data(Data[1]), .Q(Q[1]));
  memoryclk memoryclk_4 (.clt(write), .Data(Data[2]), .Q(Q[2]));
  memoryclk memoryclk_5 (.clt(write), .Data(Data[3]), .Q(Q[3]));
  memoryclk memoryclk_6 (.clt(write), .Data(Data[4]), .Q(Q[4]));
  memoryclk memoryclk_7 (.clt(write), .Data(Data[5]), .Q(Q[5]));
  memoryclk memoryclk_8 (.clt(write), .Data(Data[7]), .Q(Q[7]));
endmodule

module reg4bit (
  input  enable,
  input  [3:0] data,
  output [3:0] Q
);

  memoryclk memoryclk_1 (.clt(enable), .Data(data[0]), .Q(Q[0]));
  memoryclk memoryclk_2 (.clt(enable), .Data(data[1]), .Q(Q[1]));
  memoryclk memoryclk_3 (.clt(enable), .Data(data[2]), .Q(Q[2]));
  memoryclk memoryclk_4 (.clt(enable), .Data(data[3]), .Q(Q[3]));
endmodule

module Incrementer4bit (
  input  [3:0] PC_input,
  output [3:0] sum
);

  wire and_1_out, and_2_out, and_3_out;

  xor xor_1 (sum[0], PC_input[0], 1'b1);
  and and_1 (and_1_out, PC_input[0], 1'b1);
  xor xor_2 (sum[1], PC_input[1], and_1_out);
  and and_2 (and_2_out, PC_input[1], and_1_out);
  xor xor_3 (sum[2], PC_input[2], and_2_out);
  and and_3 (and_3_out, PC_input[2], and_2_out);
  xor xor_4 (sum[3], PC_input[3], and_3_out);
endmodule

module BusMux2waybit1 (
  input  Incrementer,
  input  PC_LOAD,
  input  Branch_Address,
  output result
);

  wire and_1_out, and_2_out, not_1_out;

  not not_1 (not_1_out, PC_LOAD);
  and and_1 (and_1_out, Incrementer, not_1_out);
  and and_2 (and_2_out, Branch_Address, PC_LOAD);
  or or_1 (result, and_1_out, and_2_out);
endmodule

module BusMux2way (
  input  S,
  input  [3:0] increment,
  input  [3:0] Branch,
  output [3:0] result
);

  BusMux2waybit1 busmux2waybit1_1 (
    .Incrementer(increment[0]), .PC_LOAD(S), .Branch_Address(Branch[0]), .result(result[0]));
  BusMux2waybit1 busmux2waybit1_2 (
    .Incrementer(increment[1]), .PC_LOAD(S), .Branch_Address(Branch[1]), .result(result[1]));
  BusMux2waybit1 busmux2waybit1_3 (
    .Incrementer(increment[2]), .PC_LOAD(S), .Branch_Address(Branch[2]), .result(result[2]));
  BusMux2waybit1 busmux2waybit1_4 (
    .Incrementer(increment[3]), .PC_LOAD(S), .Branch_Address(Branch[3]), .result(result[3]));
endmodule

module PC (
  input  load,
  input  [3:0] jump_address,
  input  jump_enb,
  output [3:0] Q
);

  wire [3:0] busmux2way_1_result, incrementer4bit_1_sum;

  reg4bit reg4bit_1 (.enable(load), .data(busmux2way_1_result), .Q(Q));
  Incrementer4bit incrementer4bit_1 (.PC_input(Q), .sum(incrementer4bit_1_sum));
  // Probe on Q
  BusMux2way busmux2way_1 (
    .S(jump_enb), .increment(incrementer4bit_1_sum), .Branch(jump_address), .result(busmux2way_1_result));
endmodule

module memorybank (
  input  enable,
  input  [3:0] W_address,
  input  [7:0] Data,
  output [7:0] Q
);

  wire decoder_1_out0, decoder_1_out1, decoder_1_out2, decoder_1_out3, decoder_1_out4, decoder_1_out5,
       decoder_1_out6, decoder_1_out7, decoder_1_out8, decoder_1_out9, decoder_1_out10, decoder_1_out11,
       decoder_1_out12, decoder_1_out13, decoder_1_out14, decoder_1_out15;
  wire [7:0] reg8bit_1_q, reg8bit_2_q, reg8bit_3_q, reg8bit_4_q, reg8bit_5_q, reg8bit_6_q, reg8bit_7_q,
       reg8bit_8_q, reg8bit_9_q, reg8bit_10_q, reg8bit_11_q, reg8bit_12_q, reg8bit_13_q, reg8bit_14_q,
       reg8bit_15_q, reg8bit_16_q;

  Decoder #(.select(4)) decoder_1 (
    .out0(decoder_1_out0), .out1(decoder_1_out1), .out2(decoder_1_out2), .out3(decoder_1_out3),
    .out4(decoder_1_out4), .out5(decoder_1_out5), .out6(decoder_1_out6), .out7(decoder_1_out7),
    .out8(decoder_1_out8), .out9(decoder_1_out9), .out10(decoder_1_out10), .out11(decoder_1_out11),
    .out12(decoder_1_out12), .out13(decoder_1_out13), .out14(decoder_1_out14), .out15(decoder_1_out15),
    .sel(W_address), .en(enable));
  // Probe on Data
  reg8bit reg8bit_1 (.write(decoder_1_out0), .Data(Data), .Q(reg8bit_1_q));
  reg8bit reg8bit_2 (.write(decoder_1_out1), .Data(Data), .Q(reg8bit_2_q));
  reg8bit reg8bit_3 (.write(decoder_1_out2), .Data(Data), .Q(reg8bit_3_q));
  reg8bit reg8bit_4 (.write(decoder_1_out3), .Data(Data), .Q(reg8bit_4_q));
  reg8bit reg8bit_5 (.write(decoder_1_out4), .Data(Data), .Q(reg8bit_5_q));
  reg8bit reg8bit_6 (.write(decoder_1_out5), .Data(Data), .Q(reg8bit_6_q));
  reg8bit reg8bit_7 (.write(decoder_1_out6), .Data(Data), .Q(reg8bit_7_q));
  reg8bit reg8bit_8 (.write(decoder_1_out7), .Data(Data), .Q(reg8bit_8_q));
  reg8bit reg8bit_9 (.write(decoder_1_out8), .Data(Data), .Q(reg8bit_9_q));
  reg8bit reg8bit_10 (.write(decoder_1_out9), .Data(Data), .Q(reg8bit_10_q));
  reg8bit reg8bit_11 (.write(decoder_1_out10), .Data(Data), .Q(reg8bit_11_q));
  reg8bit reg8bit_12 (.write(decoder_1_out11), .Data(Data), .Q(reg8bit_12_q));
  reg8bit reg8bit_13 (.write(decoder_1_out12), .Data(Data), .Q(reg8bit_13_q));
  reg8bit reg8bit_14 (.write(decoder_1_out13), .Data(Data), .Q(reg8bit_14_q));
  reg8bit reg8bit_15 (.write(decoder_1_out14), .Data(Data), .Q(reg8bit_15_q));
  reg8bit reg8bit_16 (.write(decoder_1_out15), .Data(Data), .Q(reg8bit_16_q));
  Multiplexer #(.select(4), .width(8)) multiplexer_1 (
    .in0(reg8bit_1_q), .in1(reg8bit_2_q), .in2(reg8bit_3_q), .in3(reg8bit_4_q), .in4(reg8bit_5_q),
    .in5(reg8bit_6_q), .in6(reg8bit_7_q), .in7(reg8bit_8_q), .in8(reg8bit_9_q), .in9(reg8bit_10_q),
    .in10(reg8bit_11_q), .in11(reg8bit_12_q), .in12(reg8bit_13_q), .in13(reg8bit_14_q), .in14(reg8bit_15_q),
    .in15(reg8bit_16_q), .out(Q), .sel(W_address));
  // Probe on Q
endmodule

module r_mux (
  input  [7:0] ALU,
  input  [7:0] Mem,
  input  [3:0] IR,
  input  s_alu,
  input  s_mem,
  input  S_ir,
  output [7:0] out_7
);

  wire and_1_out, and_2_out, and_3_out, and_4_out, and_5_out, and_6_out, and_7_out, and_8_out, and_9_out,
       and_10_out, and_11_out, and_12_out, and_13_out, and_14_out, and_15_out, and_16_out, and_17_out,
       and_18_out, and_19_out, and_20_out, and_21_out, and_22_out, and_23_out, and_24_out;

  and and_1 (and_1_out, S_ir, IR[3]);
  and and_2 (and_2_out, S_ir, 1'b0);
  and and_3 (and_3_out, s_mem, Mem[3]);
  and and_4 (and_4_out, s_mem, Mem[7]);
  and and_5 (and_5_out, s_alu, ALU[3]);
  and and_6 (and_6_out, s_alu, ALU[7]);
  or or_1 (out_7[3], and_5_out, and_3_out, and_1_out);
  or or_2 (out_7[7], and_6_out, and_4_out, and_2_out);
  and and_7 (and_7_out, S_ir, IR[2]);
  and and_8 (and_8_out, S_ir, 1'b0);
  and and_9 (and_9_out, s_mem, Mem[6]);
  and and_10 (and_10_out, s_mem, Mem[2]);
  and and_11 (and_11_out, s_alu, ALU[2]);
  or or_3 (out_7[2], and_11_out, and_10_out, and_7_out);
  and and_12 (and_12_out, s_alu, ALU[6]);
  or or_4 (out_7[6], and_12_out, and_9_out, and_8_out);
  and and_13 (and_13_out, S_ir, IR[1]);
  and and_14 (and_14_out, s_mem, Mem[1]);
  and and_15 (and_15_out, S_ir, 1'b0);
  and and_16 (and_16_out, s_mem, Mem[5]);
  and and_17 (and_17_out, s_alu, ALU[1]);
  or or_5 (out_7[1], and_17_out, and_14_out, and_13_out);
  and and_18 (and_18_out, s_alu, ALU[5]);
  and and_19 (and_19_out, S_ir, 1'b0);
  or or_6 (out_7[5], and_18_out, and_16_out, and_15_out);
  and and_20 (and_20_out, s_mem, Mem[0]);
  and and_21 (and_21_out, S_ir, IR[0]);
  and and_22 (and_22_out, s_mem, Mem[4]);
  and and_23 (and_23_out, s_alu, ALU[0]);
  or or_7 (out_7[0], and_23_out, and_20_out, and_21_out);
  and and_24 (and_24_out, s_alu, ALU[4]);
  or or_8 (out_7[4], and_24_out, and_22_out, and_19_out);
endmodule

module Final_milston2 (
  input  RUN,
  input  in_2,
  input  [3:0] opcode
);

  wire clock_control_1_execute_w, clock_control_1_fetch, clock_control_1_fetch_w, not_1_out, undriven,
       undriven_2, undriven_3, undriven_4;
  wire [3:0] busmux2way_1_result, IR_q, pc_1_q;
  wire [7:0] final_1_out_9, MEMORY_q, r_mux_1_out_7, R_q;

  not not_1 (not_1_out, in_2);
  clock_control clock_control_1 (
    .RUN(RUN), .halt(not_1_out), .fetch(clock_control_1_fetch), .fetch_w(clock_control_1_fetch_w),
    .execute_w(clock_control_1_execute_w));  // open: Cl, execute
  FINAL final_1 (.A(R_q), .out_9(final_1_out_9));  // open: B, ADD, SUB, XOR_r, AND_r, R_shift_r, L_shift_l
  r_mux r_mux_1 (
    .ALU(final_1_out_9), .Mem(MEMORY_q), .IR(IR_q), .s_alu(undriven), .s_mem(undriven_2), .S_ir(undriven_3),
    .out_7(r_mux_1_out_7));
  reg8bit R (.Data(r_mux_1_out_7), .Q(R_q));  // open: write
  reg8bit IR (.write(clock_control_1_fetch_w), .Data(MEMORY_q), .Q({opcode, IR_q}));
  PC pc_1 (.load(undriven_4), .jump_address(IR_q), .jump_enb(clock_control_1_execute_w), .Q(pc_1_q));
  BusMux2way busmux2way_1 (.S(clock_control_1_fetch), .increment(IR_q), .Branch(pc_1_q), .result(busmux2way_1_result));
  memorybank MEMORY (.W_address(busmux2way_1_result), .Data(R_q), .Q(MEMORY_q));  // open: enable
endmodule
